# Fritzing sketch cablage_plaques_cuivres (saved by Fritzing 0.9.4)
stripboards: 10

parts:
  Part1 = Arduino Mega 2560 (Rev3)
  LED1 = RGB LED (com. cathode, rgb) [package="5 mm [THT]"]
  LED2 = RGB LED (com. cathode, rgb) [package="5 mm [THT]"]
  LED3 = RGB LED (com. cathode, rgb) [package="5 mm [THT]"]
  LED4 = RGB LED (com. cathode, rgb) [package="5 mm [THT]"]
  R10 = PHOTOCELL [package=photocell]
  U7 = POT [package=pot_alpha_rv16af-20]
  RHT2 = Humidity and Temperature Sensor RHT03
  R11 = Resistor [tolerance=±5% resistance=220 package=THT]
  S3 = Pushbutton [package="[THT]"]
  U8 = SWITCH_SPDT [package=kps-1290]
  R12 = Resistor [tolerance=±5% resistance=220 package=THT]  # not connected
  R13 = Resistor [tolerance=±5% resistance=220 package=THT]  # not connected
  R14 = Resistor [tolerance=±5% resistance=220 package=THT]  # not connected
  Grove1 = Grove OLED 128x96

nets:
  N1: Part1.A14, Grove1.SCL
  N2: Part1.A15, Grove1.SDA
  N3: Part1.A6, RHT2.GND_1
  3V3: Part1.3V3, Part1.5V, U7.E, R11.Pin_1, Grove1.VCC
  GND: Part1.GND, R10.P$2, RHT2.GND_2, S3.Pin_3, S3.Pin_4, U8.O, Grove1.GND
  N4: LED1.red_anode, LED2.red_anode, LED3.red_anode, LED4.red_anode
  N5: LED1.common_cathode, LED3.common_cathode
  N6: LED1.green_anode, LED3.green_anode
  N7: LED1.blue_anode, LED3.blue_anode
  N8: LED2.common_cathode, LED4.common_cathode
  N9: LED2.green_anode, LED4.green_anode
  N10: LED2.blue_anode, LED4.blue_anode
  N11: R10.P$1, U7.S
  N12: RHT2.Vcc, U8.P
  N13: RHT2.Data-signal, R11.Pin_0

notes:
  OLED
  LED RGB
  Module LEDs
  Capteur luminosité
  Capteur de température
  Bouton
  Interrupteur
