# Fritzing sketch cablage_arduino_fritzing (saved by Fritzing 0.9.4)
breadboards: 2

parts:
  Composant1 = Arduino Mega 2560 (Rev3)
  Grove1 = Grove OLED 128x96
  S2 = Pushbutton [package="[THT]"]
  LED2 = RGB LED (com. anode, rbg) [package="5 mm [THT]"]
  U1 = POT [package=pot_alpha_rv16af-20]  # not connected
  RHT1 = Humidity and Temperature Sensor RHT03
  R2 = Resistor [tolerance=±5% resistance=220 package=THT]
  U4 = LM 358 Dual Op-Amp [package="DIP8 [THT]"]
  U5 = OP27 - Low Noise, Precision Op Amp [part_number=OP27]
  P2 = S1133 Si Photodiode [package="8mm Ceramic [THT]"]
  R3 = Resistor [tolerance=±5% resistance=24k package="2512 [SMD]"]
  R4 = Resistor [tolerance=±5% resistance=220k package="2512 [SMD]"]
  R5 = Resistor [tolerance=±5% resistance=100 package="2512 [SMD]"]
  R6 = Resistor [tolerance=±5% resistance=220 package=THT]
  R7 = Resistor [tolerance=±5% resistance=220 package=THT]
  R8 = Resistor [tolerance=±5% resistance=220 package=THT]
  R9 = Resistor [tolerance=±5% resistance=100 package=THT]
  Mod3 = laser receiver [package=THT]
  Mod4 = KY-008 Laser Transmitter Module [package="Breakout board"]

nets:
  N1: Composant1.A0, Grove1.SDA
  N2: Composant1.A1, Grove1.SCL
  N3: Composant1.A2, U4.connector0, R4.Pin_0
  3V3: Composant1.3V3, Grove1.VCC
  5V: Composant1.5V, LED2.common_anode, RHT1.Vcc, R2.Pin_0, U4.connector7, U5.V+, R9.Pin_0, Mod3.pin3
  GND: Composant1.GND, Composant1.D4_PWM, Grove1.GND, S2.Pin_3, S2.Pin_4, RHT1.GND_2, U4.connector3, U5.+IN, U5.-V, P2.cathode, R3.Pin_1, Mod4.-
  N4: Composant1.D2_PWM, Mod3.pin2
  N5: Composant1.D3_PWM, RHT1.GND_1
  N6: Composant1.D5_PWM, R6.Pin_1
  N7: Composant1.D6_PWM, R7.Pin_1
  N8: Composant1.D7_PWM, R8.Pin_1
  N9: S2.Pin_1, S2.Pin_2
  N10: LED2.red_cathode, R6.Pin_0
  N11: LED2.blue_cathode, R7.Pin_0
  N12: LED2.green_cathode, R8.Pin_0
  N13: RHT1.Data-signal, R2.Pin_1
  N14: U4.connector1, R3.Pin_0, R4.Pin_1
  N15: U4.connector2, U5.OUT, R5.Pin_0
  N16: U5.-IN, P2.anode
  N17: R9.Pin_1, Mod4.S

custom parts:
  laser receiver: Generic non modulated laser receiver module.
  KY-008 Laser Transmitter Module: KY-008 Laser Transmitter Module, emits a dot shaped red laser beam.
