# Fritzing sketch cablage_arduino_fritzing_v2 (saved by Fritzing 0.9.4)
breadboards: 2

parts:
  Composant1 = Arduino Mega 2560 (Rev3)
  Grove1 = Grove OLED 128x96
  S2 = Pushbutton [package="[THT]"]
  LED2 = RGB LED (com. anode, rbg) [package="5 mm [THT]"]
  RHT1 = Humidity and Temperature Sensor RHT03
  R2 = Resistor [tolerance=±5% resistance=220 package=THT]
  R6 = Resistor [tolerance=±5% resistance=220 package=THT]
  R7 = Resistor [tolerance=±5% resistance=220 package=THT]
  R8 = Resistor [tolerance=±5% resistance=220 package=THT]
  U6 = POT [package=pot_alpha_rv16af-20]
  R9 = PHOTOCELL [package=photocell]
  U7 = SWITCH_SPDT [package=kps-1290]

nets:
  N1: Composant1.A0, Grove1.SDA
  N2: Composant1.A1, Grove1.SCL
  N3: Composant1.A2, U6.S, R9.P$1
  3V3: Composant1.3V3, Grove1.VCC
  5V: Composant1.5V, LED2.common_anode, RHT1.Vcc, R2.Pin_0, U6.E, U7.P
  GND: Composant1.GND, Composant1.D4_PWM, Grove1.GND, S2.Pin_3, S2.Pin_4, RHT1.GND_2, R9.P$2, U7.O
  N4: Composant1.D2_PWM, U7.S
  N5: Composant1.D3_PWM, RHT1.GND_1
  N6: Composant1.D5_PWM, R6.Pin_1
  N7: Composant1.D6_PWM, R7.Pin_1
  N8: Composant1.D7_PWM, R8.Pin_1
  N9: S2.Pin_1, S2.Pin_2
  N10: LED2.red_cathode, R6.Pin_0
  N11: LED2.blue_cathode, R7.Pin_0
  N12: LED2.green_cathode, R8.Pin_0
  N13: RHT1.Data-signal, R2.Pin_1
