# Fritzing sketch cablage_plaques_cuivres (saved by Fritzing 0.9.4)
stripboards: 16

parts:
  Part1 = Arduino Mega 2560 (Rev3)
  LED1 = RGB LED (com. cathode, rgb) [package="5 mm [THT]"]
  LED2 = RGB LED (com. cathode, rgb) [package="5 mm [THT]"]
  LED3 = RGB LED (com. cathode, rgb) [package="5 mm [THT]"]
  LED4 = RGB LED (com. cathode, rgb) [package="5 mm [THT]"]
  R10 = PHOTOCELL [package=photocell]
  U7 = POT [package=pot_alpha_rv16af-20]
  RHT2 = Humidity and Temperature Sensor RHT03
  R11 = Resistor [tolerance=±5% resistance=220 package=THT]
  S3 = Pushbutton [package="[THT]"]
  U8 = SWITCH_SPDT [package=kps-1290]  # not connected

nets:
  3V3: Part1.3V3, Part1.5V
  N1: LED1.red_anode, LED2.red_anode, LED3.red_anode, LED4.red_anode
  N2: LED1.common_cathode, LED3.common_cathode
  N3: LED1.green_anode, LED3.green_anode
  N4: LED1.blue_anode, LED3.blue_anode
  N5: LED2.common_cathode, LED4.common_cathode
  N6: LED2.green_anode, LED4.green_anode
  N7: LED2.blue_anode, LED4.blue_anode
  N8: R10.P$1, U7.S
  N9: RHT2.Vcc, R11.Pin_0
  N10: RHT2.Data-signal, R11.Pin_1
  N11: S3.Pin_1, S3.Pin_2, S3.Pin_3, S3.Pin_4

notes:
  OLED
  LED RGB
  Module LEDs
  Module capteur luminosité
  Module capteur de température
  Bouton
  Interrupteur
